# Fritzing sketch arhorcado (saved by Fritzing 0.9.2b)
breadboards: 1
perfboards: 1

parts:
  LED1 = LED - 3mm [color="Red (633nm)" package="3 mm [THT]"]  # not connected
  LED2 = LED - 3mm [color="Red (633nm)" package="3 mm [THT]"]  # not connected
  LED3 = LED - 3mm [color="Red (633nm)" package="3 mm [THT]"]  # not connected
  LED4 = LED - 3mm [color="Red (633nm)" package="3 mm [THT]"]  # not connected
  LED5 = LED - 3mm [color="Red (633nm)" package="3 mm [THT]"]  # not connected
  LED6 = LED - 3mm [color="Red (633nm)" package="3 mm [THT]"]  # not connected
  LED7 = LED - 3mm [color="Red (633nm)" package="3 mm [THT]"]  # not connected
  LED8 = LED - 3mm [color="Red (633nm)" package="3 mm [THT]"]  # not connected
  LED9 = LED - 3mm [color="Red (633nm)" package="3 mm [THT]"]  # not connected
  LED10 = LED - 3mm [color="Red (633nm)" package="3 mm [THT]"]  # not connected
  LED11 = LED - 3mm [color="Red (633nm)" package="3 mm [THT]"]  # not connected
  LED12 = LED - 3mm [color="Red (633nm)" package="3 mm [THT]"]  # not connected
  LED13 = LED - 3mm [color="Red (633nm)" package="3 mm [THT]"]  # not connected
  LED14 = LED - 3mm [color="Red (633nm)" package="3 mm [THT]"]  # not connected
  LED15 = LED - 3mm [color="Red (633nm)" package="3 mm [THT]"]  # not connected
  LED16 = LED - 3mm [color="Red (633nm)" package="3 mm [THT]"]  # not connected
  LED17 = LED - 3mm [color="Green (555nm)" package="3 mm [THT]"]  # not connected
  LED18 = LED - 3mm [color="Green (555nm)" package="3 mm [THT]"]  # not connected
  LED19 = LED - 3mm [color="Green (555nm)" package="3 mm [THT]"]  # not connected
  LED20 = LED - 3mm [color="Green (555nm)" package="3 mm [THT]"]  # not connected
  LED21 = LED - 3mm [color="Green (555nm)" package="3 mm [THT]"]  # not connected
  LED22 = LED - 3mm [color="Green (555nm)" package="3 mm [THT]"]  # not connected
  LED23 = LED - 3mm [color="Green (555nm)" package="3 mm [THT]"]  # not connected
  LED24 = LED - 3mm [color="Green (555nm)" package="3 mm [THT]"]  # not connected
  LED25 = LED - 3mm [color="Green (555nm)" package="3 mm [THT]"]  # not connected
  LED26 = LED - 3mm [color="Green (555nm)" package="3 mm [THT]"]  # not connected
  LED27 = LED - 3mm [color="Green (555nm)" package="3 mm [THT]"]  # not connected
  LED28 = LED - 3mm [color="Green (555nm)" package="3 mm [THT]"]  # not connected
  LED29 = LED - 3mm [color="Green (555nm)" package="3 mm [THT]"]  # not connected
  LED30 = LED - 3mm [color="Green (555nm)" package="3 mm [THT]"]  # not connected
  LED31 = LED - 3mm [color="Green (555nm)" package="3 mm [THT]"]  # not connected
  Part1 = Arduino Mega ADK (Rev3)
  LCD1 = LCD screen
  R1 = Rotary Potentiometer (Small) [maximum_resistance=100kΩ package=THT]
  S1 = Pushbutton [package="[THT]"]
  S2 = Pushbutton [package="[THT]"]
  S3 = Pushbutton [package="[THT]"]
  R2 = Resistor [tolerance=±5% resistance=10k package=THT]
  R3 = Resistor [tolerance=±5% resistance=10k package=THT]
  R4 = Resistor [tolerance=±5% resistance=10k package=THT]
  R5 = Resistor [tolerance=±5% resistance=220 package=THT]

nets:
  N1: Part1.D9_PWM, LCD1.RS
  N2: Part1.D8_PWM, LCD1.E
  N3: Part1.5V, LCD1.LED+, R1.leg1, S1.Pin_1, S1.Pin_2, S2.Pin_1, S2.Pin_2, S3.Pin_1, S3.Pin_2, R5.Pin_0
  GND: Part1.GND, LCD1.VSS, LCD1.R/W, LCD1.LED-, R1.leg2, R2.Pin_0, R3.Pin_0, R4.Pin_0
  N4: Part1.D2_PWM, LCD1.DB7
  N5: Part1.D3_PWM, LCD1.DB6
  N6: Part1.D5_PWM, LCD1.DB5
  N7: Part1.D6_PWM, LCD1.DB4
  N8: Part1.D39, S1.Pin_3, S1.Pin_4, R4.Pin_1
  N9: Part1.D40, S2.Pin_3, S2.Pin_4, R2.Pin_1
  N10: Part1.D41, S3.Pin_3, S3.Pin_4, R3.Pin_1
  N11: LCD1.VDD, R5.Pin_1
  N12: LCD1.V0, R1.wiper
